# Fritzing sketch NuPogodi (saved by Fritzing 0.9.3b)
breadboards: 2

parts:
  LCD1 = 2.8" SPI TFT Module [part_number=MSP2807]
  Mod1 = Raspberry Pi Pico W
  S1 = lock switch 8x8
  S2 = Pushbutton [package="[THT]"]
  S4 = Pushbutton [package="[THT]"]
  S5 = Pushbutton [package="[THT]"]
  S6 = Pushbutton [package="[THT]"]
  S7 = Pushbutton [package="[THT]"]
  S8 = Pushbutton [package="[THT]"]
  S9 = Pushbutton [package="[THT]"]
  R1 = Resistor [tolerance=±5% resistance=1k package=THT]
  buz1 = Piezo Buzzer
  S10 = Pushbutton [package="[THT]"]
  R2 = Resistor [tolerance=±5% resistance=100 package=THT]
  Q3 = NPN-Transistor [part_number=2N2222 package="TO92 [THT]"]

nets:
  N1: LCD1.pin1, LCD1.pin8, Mod1.pin_36, S1.Pin_2, S1.Pin_5, R2.Pin_1
  N2: LCD1.pin2, Mod1.pin_3, Mod1.pin_8, Mod1.pin_13, Mod1.pin_18, Mod1.pin_23, Mod1.pin_28, Mod1.pin_33, Mod1.pin_38, Mod1.pin_42, Q3.E
  N3: LCD1.pin3, Mod1.pin_22
  N4: LCD1.pin4, Mod1.pin_27
  N5: LCD1.pin5, Mod1.pin_26
  N6: LCD1.pin6, Mod1.pin_25
  N7: LCD1.pin7, Mod1.pin_24
  N8: LCD1.pin9, Mod1.pin_21
  N9: Mod1.pin_9, S7.Pin_3, S7.Pin_4, S8.Pin_3, S8.Pin_4, S9.Pin_3, S9.Pin_4, S10.Pin_3, S10.Pin_4
  N10: Mod1.pin_10, S2.Pin_3, S2.Pin_4, S4.Pin_3, S4.Pin_4, S5.Pin_3, S5.Pin_4, S6.Pin_3, S6.Pin_4
  N11: Mod1.pin_11, S1.Pin_1, S1.Pin_6
  N12: Mod1.pin_14, S9.Pin_1, S9.Pin_2
  N13: Mod1.pin_15, S7.Pin_1, S7.Pin_2
  N14: Mod1.pin_16, S8.Pin_1, S8.Pin_2
  N15: Mod1.pin_17, S10.Pin_1, S10.Pin_2
  N16: Mod1.pin_20, R1.Pin_0
  N17: S1.Pin_3, S1.Pin_4
  N18: S2.Pin_1, S2.Pin_2
  N19: S4.Pin_1, S4.Pin_2
  N20: S5.Pin_1, S5.Pin_2
  N21: S6.Pin_1, S6.Pin_2
  N22: R1.Pin_1, Q3.B
  N23: buz1.pin_1, Q3.C
  N24: buz1.pin_2, R2.Pin_0

custom parts:
  2.8" SPI TFT Module: A generic 2.8 inch LCD TFT 320x240 display with touchscreen and SD card slot. Uses the ILI9341 controller, like the Adafruit displays of this size uses.
  Raspberry Pi Pico W: Raspberry Pi Pico W. Based around the RP2040 microcontroller the Pico W is a low cost microcontroller device bringing Raspberry Pi quality, cost, and easy of use to the microcontroller space. The areas marked KEEPOUT in pcb silkscreen should not have traces running through them to avoid shorts on a soldered in module!
  lock switch 8x8: lock switch 8x8.
  Piezo Buzzer: Part from https://www.nutsvolts.com/magazine/article/november2012_SmileysWorkshop. Breadboard and icon images modified to be 0.3" in spacing and be more similar to the actual physical part.
